// Logisim project 103_AdderSubtractor.circ as structural Verilog: 1 circuit, main circuit main
module main (
);

  wire multiplexer_1_out, nand_1_out, nand_2_out, nand_3_out, nand_4_out, nand_5_out, nand_6_out, nand_7_out,
       nand_8_out, nand_9_out, nand_10_out;

  nand nand_1 (nand_1_out, 1'b1, 1'b1);
  Multiplexer multiplexer_1 (.in0(1'b1), .in1(nand_1_out), .out(multiplexer_1_out), .sel(1'b1));  // open: en
  nand nand_2 (nand_2_out, 1'b1, multiplexer_1_out);
  nand nand_3 (nand_3_out, 1'b1, nand_2_out);
  nand nand_4 (nand_4_out, nand_2_out, multiplexer_1_out);
  nand nand_5 (nand_5_out, nand_3_out, nand_4_out);
  nand nand_6 (nand_6_out, nand_5_out, 1'b1);
  nand nand_7 (nand_7_out, nand_5_out, nand_6_out);
  nand nand_8 (nand_8_out, nand_6_out, 1'b1);
  nand nand_9 (nand_9_out, nand_6_out, nand_2_out);
  nand nand_10 (nand_10_out, nand_7_out, nand_8_out);
  // Probe on nand_10_out
  // Probe on nand_9_out

  // Notes on the sheet:
  //   Sub
  //   Adder Subtractor
endmodule
